# Fritzing sketch Blink (saved by Fritzing 0.9.3b)
circuit board: 6.88566cm x 5.36311cm

parts:
  LED = LED - 5mm [color="Red (633nm)" package="5 mm [THT]"]
  Arduino1 = Arduino Uno (Rev3)
  RHT1 = Humidity and Temperature Sensor RHT03

nets:
  N1: LED.cathode, Arduino1.GND, RHT1.GND_2
  N2: LED.anode, Arduino1.D13/SCK
  N3: Arduino1.D2, RHT1.Data-signal
  5V: Arduino1.5V, RHT1.Vcc

notes:
  BLINK
  VCC
  DATA PIN
  GND
  LED
  DHT11

// code stored in the sketch: Blink.ino
/*
  Blink
  
  Switching a LED on and off
  
  This example is part of the Fritzing Creator Kit: www.fritzing.org/creator-kit.
*/

int led = 13;                   // integer variable led is declared

void setup() {                  // the setup() method is executed only once
  pinMode(led, OUTPUT);         // the led PIN is declared as digital output
}

void loop() {                   // the loop() method is repeated
  digitalWrite(led, HIGH);      // switching on the led 
  delay(1000);                  // stopping the program for 1000 milliseconds
  digitalWrite(led, LOW);       // switching off the led 
  delay(1000);                  // stopping the program for 1000 milliseconds
}
